# Fritzing sketch Untitled Sketch (saved by Fritzing 1.0.4)
breadboards: 1

parts:
  A1 = Particle - Photon2
  Load_Cell1 = Load Cell - Red/white/black/green
  Part1 = HX711 Weighing Sensor Module
  U1 = ENCODER_RGB [package=encoder_led_2]
  OLED_I2C1 = OLED 128x64 I2C Monochrome Display
  S1 = Square Pushbutton

nets:
  VCC: A1.Pin_2, A1.Pin_31, Part1.VCC, U1.+, OLED_I2C1.VDD, S1.leg0
  GND: A1.Pin_4, A1.Pin_30, A1.Pin_35, Part1.GND, U1.C, OLED_I2C1.GND
  N1: A1.Pin_11, Part1.DO/RX
  N2: A1.Pin_12, Part1.CK/TX
  N3: A1.Pin_14, U1.B
  N4: A1.Pin_15, U1.A
  N5: A1.Pin_17, OLED_I2C1.SDA
  N6: A1.Pin_18, OLED_I2C1.SCK
  N7: A1.Pin_22, S1.leg1
  N8: Load_Cell1.wire1, Part1.E+
  N9: Load_Cell1.wire2, Part1.E-
  N10: Load_Cell1.wire3, Part1.A+
  N11: Load_Cell1.wire4, Part1.A-

custom parts:
  Particle - Photon2: The Photon 2 is a microcontroller and Wi-Fi networking developed by particle. Features: 802.11a/b/g/n Wi-Fi, 2.4 GHz and 5 GHz Integrated PCB antenna Integrated U.FL connector for external antenna Integrated RF switch BLE 5 using same antenna as Wi-Fi Realtek RTL8721DM MCU ARM Cortex M33 CPU, 200 MHz 2048 KB (2 MB) user application maximum size 3072 KB (3 MB) of RAM available to user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
  Load Cell - Red/white/black/green: A rectangle load cell/weighting pressure Sensor with four wires - Red, white, black, green. Normally corresponding with E+, E-, A+, A- respectively.
  ENCODER_RGB: SparkFun RGB rotary Encoder
